# Fritzing sketch ESP32_PCB_A_002_b (saved by Fritzing 0.9.3b)
stripboards: 1

parts:
  J1 = female pin header, 19 pins [form="♀ (female)"]
  J2 = female pin header, 19 pins [form="♀ (female)"]
  J3 = male pin header, 5 pins [form="♂ (male)"]
  J4 = male pin header, 5 pins [form="♂ (male)"]
  J5 = male pin header, 5 pins [form="♂ (male)"]
  J6 = male pin header, 5 pins [form="♂ (male)"]
  J7 = male pin header, 9 pins [form="♂ (male)"]
  J8 = male pin header, 9 pins [form="♂ (male)"]
  J9 = male pin header, 9 pins [form="♂ (male)"]
  J10 = male pin header, 9 pins [form="♂ (male)"]
  J11 = male pin header, 12 pins [form="♂ (male)"]
  J12 = male pin header, 12 pins [form="♂ (male)"]
  J13 = male pin header, 12 pins [form="♂ (male)"]
  J14 = male pin header, 12 pins [form="♂ (male)"]
  J15 = male pin header, 4 pins [form="♂ (male)"]
  J16 = male pin header, 2 pins [form="♂ (male)"]
  J17 = male pin header, 2 pins [form="♂ (male)"]
  J18 = male pin header, 6 pins [form="♂ (male)"]
  J19 = male pin header, 6 pins [form="♂ (male)"]
  J20 = male pin header, 6 pins [form="♂ (male)"]
  J21 = female pin header, 8 pins [form="♀ (female)"]
  J22 = female pin header, 8 pins [form="♀ (female)"]
  J24 = male pin header, 8 pins [form="♂ (male)"]
  J23 = male pin header, 8 pins [form="♂ (male)"]
  S1 = Pushbutton [package=THT]
  S2 = Pushbutton [package=THT]
  RE1 = Rotary Encoder [package=THT]
  J25 = male pin header, 3 pins [form="♂ (male)"]
  J26 = male pin header, 3 pins [form="♂ (male)"]
  J27 = male pin header, 2 pins [form="♂ (male)"]
  J28 = male pin header, 2 pins [form="♂ (male)"]
  J29 = male pin header, 2 pins [form="♂ (male)"]
  J30 = male pin header, 2 pins [form="♂ (male)"]
  J31 = male pin header, 2 pins [form="♂ (male)"]
  J32 = male pin header, 2 pins [form="♂ (male)"]
  J33 = male pin header, 2 pins [form="♂ (male)"]
  J34 = male pin header, 2 pins [form="♂ (male)"]
  J35 = male pin header, 2 pins [form="♂ (male)"]
  J36 = male pin header, 2 pins [form="♂ (male)"]

nets:
  N1: J1.pin1, J1.pin7, J2.pin14, J5.pin1, J5.pin2, J5.pin3, J5.pin4, J5.pin5, J7.pin1, J7.pin2, J7.pin3, J7.pin4, J7.pin5, J7.pin6, J7.pin7, J7.pin8, J7.pin9, J14.pin1, J14.pin2, J14.pin3, J14.pin4, J14.pin5, J14.pin6, J14.pin7, J14.pin8, J14.pin9, J14.pin10, J14.pin11, J14.pin12, J15.pin4, J18.pin3, J19.pin3, J20.pin3
  N2: J1.pin2, J3.pin1, J6.pin1
  N3: J1.pin3, J3.pin2, J6.pin2
  N4: J1.pin4, J3.pin3, J6.pin3
  N5: J1.pin5, J3.pin4, J6.pin4
  N6: J1.pin6, J3.pin5, J6.pin5
  N7: J1.pin8, J9.pin1, J10.pin1
  N8: J1.pin9, J9.pin2, J10.pin2
  N9: J1.pin10, J9.pin3, J10.pin3
  N10: J1.pin11, J9.pin4, J10.pin4
  N11: J1.pin12, J9.pin5, J10.pin5
  N12: J1.pin13, J9.pin6, J10.pin6
  N13: J1.pin14, J9.pin7, J10.pin7
  N14: J1.pin15, J9.pin8, J10.pin8
  N15: J1.pin16, J9.pin9, J10.pin9
  N16: J2.pin1, J17.pin2
  N17: J2.pin2, J11.pin1, J12.pin1
  N18: J2.pin3, J11.pin2, J12.pin2
  N19: J2.pin4, J11.pin3, J12.pin3
  N20: J2.pin5, J11.pin4, J12.pin4
  N21: J2.pin6, J11.pin5, J12.pin5
  N22: J2.pin7, J11.pin6, J12.pin6
  N23: J2.pin8, J11.pin7, J12.pin7
  N24: J2.pin9, J11.pin8, J12.pin8
  N25: J2.pin10, J11.pin9, J12.pin9
  N26: J2.pin11, J11.pin10, J12.pin10
  N27: J2.pin12, J11.pin11, J12.pin11
  N28: J2.pin13, J11.pin12, J12.pin12
  N29: J2.pin15, J15.pin1, J15.pin2
  N30: J2.pin19, J16.pin1, J16.pin2
  N31: J4.pin1, J4.pin2, J4.pin3, J4.pin4, J4.pin5, J8.pin1, J8.pin2, J8.pin3, J8.pin4, J8.pin5, J8.pin6, J8.pin7, J8.pin8, J8.pin9, J13.pin1, J13.pin2, J13.pin3, J13.pin4, J13.pin5, J13.pin6, J13.pin7, J13.pin8, J13.pin9, J13.pin10, J13.pin11, J13.pin12, J15.pin3, J17.pin1, J18.pin4, J19.pin4, J20.pin4
  N32: J18.pin1, J18.pin2
  N33: J18.pin5, J18.pin6
  N34: J19.pin1, J19.pin2
  N35: J19.pin5, J19.pin6
  N36: J20.pin1, J20.pin2
  N37: J20.pin5, J20.pin6
  N38: J21.pin1, J22.pin1, J24.pin1, J23.pin1
  N39: J21.pin2, J22.pin2, J24.pin2, J23.pin2
  N40: J21.pin3, J22.pin3, J24.pin3, J23.pin3
  N41: J21.pin4, J22.pin4, J24.pin4, J23.pin4
  N42: J21.pin5, J22.pin5, J24.pin5, J23.pin5
  N43: J21.pin6, J22.pin6, J24.pin6, J23.pin6
  N44: J21.pin7, J22.pin7, J24.pin7, J23.pin7
  N45: J21.pin8, J22.pin8, J24.pin8, J23.pin8
  N46: S1.leg0, J32.pin1, J32.pin2
  N47: S1.leg1, J31.pin1, J31.pin2
  N48: S2.leg0, J30.pin1, J30.pin2
  N49: S2.leg1, J29.pin1, J29.pin2
  N50: RE1.EncoderPinA, J27.pin1, J27.pin2
  N51: RE1.EncoderPinB, J28.pin1, J28.pin2
  N52: J25.pin1, J26.pin1
  N53: J25.pin2, J26.pin2
  N54: J25.pin3, J26.pin3
  N55: J33.pin1, J33.pin2
  N56: J34.pin1, J34.pin2
  N57: J35.pin1, J35.pin2
  N58: J36.pin1, J36.pin2
